# Fritzing sketch pir (saved by Fritzing 0.9.3b)

parts:
  Sensore_PIR_HC-SR501 = HC-SR501 Body Sensor Module
  Part1 = Arduino Ethernet Shield (Rev3)

nets:
  VCC: Sensore_PIR_HC-SR501.VCC, Part1.3V3
  N1: Sensore_PIR_HC-SR501.OUT, Part1.ETH_CS
  GND: Sensore_PIR_HC-SR501.GND, Part1.GND

custom parts:
  HC-SR501 Body Sensor Module: Pyroelectric Infrared PIR Motion Sensor Detector Module
