# Fritzing sketch sonic (saved by Fritzing 0.9.3b)

parts:
  Part2 = SRF05 Ultrasonic Rangefinder
  Part3 = Arduino Prototyping Shield  # not connected
  Part3_2 = Arduino Ethernet Shield (Rev3)

nets:
  GND: Part2.GND, Part3_2.GND
